// Logisim project ex1.circ as structural Verilog: 4 circuits, main circuit main
module main (
  output [7:0] non_pipe_out,
  output [7:0] pipe_out
);

  wire CLK_out;
  wire [7:0] Address_Counter_q, rom_1_data;

  Counter Address_Counter (.clk(CLK_out), .Q(Address_Counter_q));  // open: clr, load, up, count, D, carry
  Clock CLK (.out(CLK_out));
  ROM rom_1 (.addr(Address_Counter_q), .data(rom_1_data));
  // Probe on non_pipe_out
  non_pipelined non_pipelined_1 (.in1(rom_1_data[3:0]), .in2(rom_1_data[7:4]), .CLK(CLK_out), .out1(non_pipe_out));
  // Probe on pipe_out
  pipelined pipelined_1 (.In1(rom_1_data[3:0]), .In2(rom_1_data[7:4]), .CLK(CLK_out), .out_4(pipe_out));

  // Notes on the sheet:
  //   contents of rom_1 (hex, n*v repeats v):
  //   13 a2 fc 8f 1c 2 b0
endmodule

module non_pipelined (
  input  [3:0] in1,
  input  [3:0] in2,
  input  CLK,
  output [7:0] out1
);

  wire [7:0] move_and_add_1_moved_multiplicand, move_and_add_1_result, move_and_add_2_moved_multiplicand,
       move_and_add_2_result, move_and_add_3_moved_multiplicand, move_and_add_3_result, move_and_add_4_result;

  pipelined pipelined_1 ();  // open: In1, In2, CLK, out_4
  // Probe on move_and_add_1_result
  move_and_add move_and_add_1 (
    .multiplier(in2[0]), .multiplicand({4'b0000, in1}), .current({8{1'b0}}), .result(move_and_add_1_result),
    .moved_multiplicand(move_and_add_1_moved_multiplicand));
  move_and_add move_and_add_2 (
    .multiplier(in2[1]), .multiplicand(move_and_add_1_moved_multiplicand), .current(move_and_add_1_result),
    .result(move_and_add_2_result), .moved_multiplicand(move_and_add_2_moved_multiplicand));
  move_and_add move_and_add_3 (
    .multiplier(in2[2]), .multiplicand(move_and_add_2_moved_multiplicand), .current(move_and_add_2_result),
    .result(move_and_add_3_result), .moved_multiplicand(move_and_add_3_moved_multiplicand));
  move_and_add move_and_add_4 (
    .multiplier(in2[3]), .multiplicand(move_and_add_3_moved_multiplicand), .current(move_and_add_3_result),
    .result(move_and_add_4_result));  // open: moved_multiplicand
  Register register_1 (.D(move_and_add_4_result), .clk(CLK), .Q(out1));  // open: en, clr
endmodule

module pipelined (
  input  [3:0] In1,
  input  [3:0] In2,
  input  CLK,
  output [7:0] out_4
);

  wire register_2_q;
  wire [7:0] move_and_add_1_moved_multiplicand, move_and_add_1_result, move_and_add_3_moved_multiplicand,
       move_and_add_3_result, move_and_add_4_result;
  wire [15:0] move_and_add_2_result;
  wire [16:0] register_1_q;

  // Probe on move_and_add_1_result
  move_and_add move_and_add_1 (
    .multiplier(In2[0]), .multiplicand({4'b0000, In1}), .current({8{1'b0}}), .result(move_and_add_1_result),
    .moved_multiplicand(move_and_add_1_moved_multiplicand));
  move_and_add move_and_add_2 (
    .multiplier(In2[1]), .multiplicand(move_and_add_1_moved_multiplicand), .current(move_and_add_1_result),
    .result(move_and_add_2_result[7:0]), .moved_multiplicand(move_and_add_2_result[15:8]));
  Register #(.width(17)) register_1 (
    .D({In2[2], move_and_add_2_result}), .clk(CLK), .Q(register_1_q));  // open: en, clr
  Register #(.width(1)) register_2 (.D(In2[3]), .clk(CLK), .Q(register_2_q));  // open: en, clr
  move_and_add move_and_add_3 (
    .multiplier(register_1_q[16]), .multiplicand(register_1_q[15:8]), .current(register_1_q[7:0]),
    .result(move_and_add_3_result), .moved_multiplicand(move_and_add_3_moved_multiplicand));
  Register register_3 (.D(move_and_add_4_result), .clk(CLK), .Q(out_4));  // open: en, clr
  move_and_add move_and_add_4 (
    .multiplier(register_2_q), .multiplicand(move_and_add_3_moved_multiplicand),
    .current(move_and_add_3_result), .result(move_and_add_4_result));  // open: moved_multiplicand
endmodule

module move_and_add (
  input  [7:0] current,
  input  [7:0] multiplicand,
  input  multiplier,
  output [7:0] result,
  output [7:0] moved_multiplicand
);

  wire [7:0] multiplexer_1_out;

  Multiplexer #(.width(8), .enable("false")) multiplexer_1 (
    .in0({8{1'b0}}), .in1(multiplicand), .out(multiplexer_1_out), .sel(multiplier));
  Adder adder_1 (.a(current), .b(multiplexer_1_out), .out(result));  // open: cin, cout
  Shifter shifter_1 (.in(multiplicand), .\dist (3'b001), .out(moved_multiplicand));
endmodule
