// Logisim project ex1.circ as structural Verilog: 1 circuit, main circuit Split
module Split (
  input  [7:0] IN1,
  input  in_2,
  output OUT1,
  output OUT2,
  output [8:0] OUT3,
  output [8:0] OUT4
);

  wire [3:0] bit_extender_2_out;
  wire [7:0] adder_2_out, register_1_q, undriven;
  wire [8:0] bit_extender_1_out, bit_extender_3_out, shifter_1_out;

  assign bit_extender_1_out = {{1{1'b0}}, IN1};  // Bit_Extender bit_extender_1
  assign bit_extender_2_out = {{3{1'b0}}, in_2};  // Bit_Extender bit_extender_2
  assign bit_extender_3_out = {{8{1'b0}}, OUT1};  // Bit_Extender bit_extender_3
  Shifter #(.width(9)) shifter_1 (.in(bit_extender_1_out), .\dist (bit_extender_2_out), .out(shifter_1_out));
  xor xor_1 (OUT1, IN1[0], IN1[1], IN1[2], IN1[3], IN1[4], IN1[5], IN1[6], IN1[7]);
  Adder #(.width(9)) adder_1 (.a(bit_extender_3_out), .b(shifter_1_out), .out(OUT3));  // open: cin, cout
  Register register_1 (.D(adder_2_out), .Q(register_1_q));  // open: en, clk, clr
  Adder adder_2 (.a(register_1_q), .b(undriven), .out(adder_2_out));  // open: cin, cout
  Comparator #(.mode("unsigned")) comparator_1 ();  // open: a, b, gt, eq, lt

  // Other names for the same wires on the sheet: IN1_0 = IN1[0]; IN1_1 = IN1[1]; IN1_2 = IN1[2]; IN1_3 = IN1[3];
  //   IN1_4 = IN1[4]; IN1_5 = IN1[5]; IN1_6 = IN1[6]; IN1_7 = IN1[7]

  // Notes on the sheet:
  //   PUT CIRCUITRY HERE
endmodule
